// Logisim project Circuitos-Display-7-Segmentos.circ as structural Verilog: 6 circuits, main circuit main
module main (
  input  in_1,
  input  in_2,
  input  c
);

  wire a_out_3, b_out_3, d_out_3, e_out_3, f_g_out_3;

  Sa a (.in_1(in_2), .in_2(in_1), .out_3(a_out_3));
  Sb b (.in_1(in_2), .in_2(in_1), .out_3(b_out_3));
  Sf_Sg f_g (.in_1(in_2), .in_2(in_1), .out_3(f_g_out_3));
  Sd d (.in_1(in_2), .in_2(in_1), .out_3(d_out_3));
  Se e (.in_1(in_2), .in_2(in_1), .out_3(e_out_3));
  _7_Segment_Display u_7_segment_display_1 (
    .g(f_g_out_3), .f(f_g_out_3), .a(a_out_3), .b(b_out_3), .e(e_out_3), .d(d_out_3), .c(c));  // open: dp
  // also tied to VCC on the sheet: c
endmodule

module Sa (
  input  in_1,
  input  in_2,
  output out_3
);

  or or_1 (out_3, in_2, in_1);
endmodule

module Sb (
  input  in_1,
  input  in_2,
  output out_3
);

  wire and_1_out, and_2_out, not_1_out, not_2_out;

  not not_1 (not_1_out, in_2);
  not not_2 (not_2_out, in_1);
  and and_1 (and_1_out, in_2, in_1);
  and and_2 (and_2_out, not_1_out, not_2_out);
  or or_1 (out_3, and_1_out, and_2_out);
endmodule

module Sd (
  input  in_1,
  input  in_2,
  output out_3
);

  xor xor_1 (out_3, in_2, in_1);
endmodule

module Se (
  input  in_1,
  input  in_2,
  output out_3
);

  wire not_1_out;

  and and_1 (out_3, in_2, not_1_out);
  not not_1 (not_1_out, in_1);
endmodule

module Sf_Sg (
  input  in_1,
  input  in_2,
  output out_3
);

  wire and_1_out;

  and and_1 (and_1_out, in_2, in_1);
  not not_1 (out_3, and_1_out);
endmodule
