// Logisim project ULA.circ as structural Verilog
module op_ADD (
  input  in_1,
  input  in_2,
  input  Carry_In,
  output out_4,
  output out_5
);

  wire and_1_out, and_2_out, xor_1_out;

  xor xor_1 (xor_1_out, in_2, in_1);
  and and_1 (and_1_out, in_2, in_1);
  and and_2 (and_2_out, xor_1_out, Carry_In);
  xor xor_2 (out_4, xor_1_out, Carry_In);
  or or_1 (out_5, and_2_out, and_1_out);

  // Notes on the sheet:
  //   Resultado
  //   Carry Out
endmodule

module op_NOR (
  input  in_1,
  input  in_2,
  output out_3
);

  nor nor_1 (out_3, in_1, in_2);
endmodule

module op_OR (
  input  in_1,
  input  in_2,
  output out_3
);

  or or_1 (out_3, in_1, in_2);
endmodule

module op_NAND (
  input  in_1,
  input  in_2,
  output out_3
);

  nand nand_1 (out_3, in_1, in_2);
endmodule

module mux_8x1 (
  input  in_1,
  input  in_2,
  input  in_3,
  input  in_4,
  input  in_5,
  input  in_6,
  input  in_7,
  input  in_8,
  input  in_9,
  input  in_10,
  input  in_11,
  output out_12
);

  wire and_1_out, and_2_out, and_3_out, and_4_out, and_5_out, and_6_out, and_7_out, and_8_out, and_9_out,
       and_10_out, and_11_out, and_12_out, and_13_out, and_14_out, and_15_out, and_16_out, not_1_out,
       not_3_out, not_4_out, not_6_out, not_7_out, not_8_out, not_10_out, not_12_out;

  not not_1 (not_1_out, in_9);
  // NOT_Gate not_2 has open pins: in=in_10, out=open
  not not_3 (not_3_out, in_11);
  not not_4 (not_4_out, in_9);
  // NOT_Gate not_5 has open pins: in=in_10, out=open
  not not_6 (not_6_out, in_9);
  not not_7 (not_7_out, in_11);
  not not_8 (not_8_out, in_9);
  // NOT_Gate not_9 has open pins: in=in_10, out=open
  not not_10 (not_10_out, in_11);
  // NOT_Gate not_11 has open pins: in=in_10, out=open
  not not_12 (not_12_out, in_11);
  and and_1 (and_1_out, not_1_out, not_3_out);
  and and_2 (and_2_out, not_4_out, in_11);
  and and_3 (and_3_out, not_6_out, not_7_out);
  and and_4 (and_4_out, not_8_out, in_11);
  and and_5 (and_5_out, in_9, not_10_out);
  and and_6 (and_6_out, in_9, in_11);
  and and_7 (and_7_out, in_9, not_12_out);
  and and_8 (and_8_out, in_9, in_11);
  and and_9 (and_9_out, in_1, and_1_out);
  and and_10 (and_10_out, in_2, and_2_out);
  and and_11 (and_11_out, in_3, and_3_out);
  and and_12 (and_12_out, in_4, and_4_out);
  and and_13 (and_13_out, in_5, and_5_out);
  and and_14 (and_14_out, in_6, and_6_out);
  and and_15 (and_15_out, in_7, and_7_out);
  and and_16 (and_16_out, in_8, and_8_out);
  or or_1 (out_12, and_9_out, and_10_out, and_11_out, and_12_out, and_13_out, and_14_out, and_15_out, and_16_out);
endmodule

module ula (
  input  [7:0] in_1,
  input  [2:0] in_2,
  input  [7:0] in_3,
  output [7:0] out_4,
  output out_5,
  output out_6
);

  wire and_1_out, and_2_out, and_3_out, and_4_out, not_1_out, not_4_out, ula_add_1_out_4, ula_sub_1_out_4;
  wire [7:0] divider_1_out, multiplier_1_out, ula_add_1_out_3, ula_nand_1_out_3, ula_nor_1_out_3,
       ula_or_1_out_3, ula_or_2_out_3, ula_sub_1_out_3;

  Multiplier multiplier_1 (.a(in_1), .b(in_3), .out(multiplier_1_out));  // open: cin, cout
  Divider divider_1 (.a(in_1), .b(in_3), .out(divider_1_out));  // open: upper, rem
  ula_NOR ula_nor_1 (.in_1(in_1), .in_2(in_3), .out_3(ula_nor_1_out_3));
  ula_ADD ula_add_1 (.in_1(in_1), .in_2(in_3), .out_3(ula_add_1_out_3), .out_4(ula_add_1_out_4));
  ula_NAND ula_nand_1 (.in_1(in_1), .in_2(in_3), .out_3(ula_nand_1_out_3));
  ula_SUB ula_sub_1 (.in_1(in_1), .in_2(in_3), .out_3(ula_sub_1_out_3), .out_4(ula_sub_1_out_4));
  ula_OR ula_or_1 (.in_1(in_1), .in_2(in_3), .out_3(ula_or_1_out_3));
  ula_OR ula_or_2 (.in_1(in_1), .in_2(in_3), .out_3(ula_or_2_out_3));
  not not_1 (not_1_out, in_2[0]);
  // NOT_Gate not_2 has open pins: in=in_2[1], out=open
  and and_1 (and_1_out, not_1_out, in_2[2]);
  // NOT_Gate not_3 has open pins: in=in_2[1], out=open
  and and_2 (and_2_out, in_2[0], not_4_out);
  not not_4 (not_4_out, in_2[2]);
  ula_mux ula_mux_1 (
    .in_1(in_2[0]), .in_2(in_2[1]), .in_3(in_2[2]), .in_4(ula_nor_1_out_3), .in_5(ula_add_1_out_3),
    .in_6(ula_nand_1_out_3), .in_7(multiplier_1_out), .in_8(ula_sub_1_out_3), .in_9(ula_or_1_out_3),
    .in_10(divider_1_out), .in_11(ula_or_2_out_3), .out_12(out_4));
  and and_3 (and_3_out, and_1_out, ula_add_1_out_4);
  and and_4 (and_4_out, and_2_out, ula_sub_1_out_4);
  flag_Z flag_z_1 (.in_1(out_4), .out_2(out_5));
  or or_1 (out_6, and_3_out, and_4_out);

  // Notes on the sheet:
  //   implementar saídas Z, C
  //   Sel.Op
  //   Se Sel.Op = soma e tiver overflow na soma
  //   Se Sel.Op = subtração e tiver overflow na subtração
  //   Resultado  Escolhido
  //   Flag C
endmodule

module ula_ADD (
  input  [7:0] in_1,
  input  [7:0] in_2,
  output [7:0] out_3,
  output out_4
);

  wire op_add_1_out_5, op_add_2_out_5, op_add_3_out_5, op_add_4_out_5, op_add_5_out_5, op_add_6_out_5,
       op_add_7_out_5, op_add_8_out_5;

  op_ADD op_add_1 (.in_1(in_1[0]), .in_2(in_2[0]), .out_4(out_3[0]), .out_5(op_add_1_out_5));  // open: Carry_In
  op_ADD op_add_2 (.in_1(in_1[1]), .in_2(in_2[1]), .Carry_In(op_add_1_out_5), .out_4(out_3[1]), .out_5(op_add_2_out_5));
  op_ADD op_add_3 (.in_1(in_1[2]), .in_2(in_2[2]), .Carry_In(op_add_2_out_5), .out_4(out_3[2]), .out_5(op_add_3_out_5));
  op_ADD op_add_4 (.in_1(in_1[3]), .in_2(in_2[3]), .Carry_In(op_add_3_out_5), .out_4(out_3[3]), .out_5(op_add_4_out_5));
  op_ADD op_add_5 (.in_1(in_1[4]), .in_2(in_2[4]), .Carry_In(op_add_4_out_5), .out_4(out_3[4]), .out_5(op_add_5_out_5));
  op_ADD op_add_6 (.in_1(in_1[5]), .in_2(in_2[5]), .Carry_In(op_add_5_out_5), .out_4(out_3[5]), .out_5(op_add_6_out_5));
  op_ADD op_add_7 (.in_1(in_1[6]), .in_2(in_2[6]), .Carry_In(op_add_6_out_5), .out_4(out_3[6]), .out_5(op_add_7_out_5));
  op_ADD op_add_8 (.in_1(in_1[7]), .in_2(in_2[7]), .Carry_In(op_add_7_out_5), .out_4(out_3[7]), .out_5(op_add_8_out_5));
  xor xor_1 (out_4, op_add_8_out_5, op_add_7_out_5);

  // Notes on the sheet:
  //   Overflow/Underflow
endmodule

module ula_NOR (
  input  [7:0] in_1,
  input  [7:0] in_2,
  output [7:0] out_3
);

  op_NOR op_nor_1 (.in_1(in_1[0]), .in_2(in_2[0]), .out_3(out_3[0]));
  op_NOR op_nor_2 (.in_1(in_1[1]), .in_2(in_2[1]), .out_3(out_3[1]));
  op_NOR op_nor_3 (.in_1(in_1[2]), .in_2(in_2[2]), .out_3(out_3[2]));
  op_NOR op_nor_4 (.in_1(in_1[3]), .in_2(in_2[3]), .out_3(out_3[3]));
  op_NOR op_nor_5 (.in_1(in_1[4]), .in_2(in_2[4]), .out_3(out_3[4]));
  op_NOR op_nor_6 (.in_1(in_1[5]), .in_2(in_2[5]), .out_3(out_3[5]));
  op_NOR op_nor_7 (.in_1(in_1[6]), .in_2(in_2[6]), .out_3(out_3[6]));
  op_NOR op_nor_8 (.in_1(in_1[7]), .in_2(in_2[7]), .out_3(out_3[7]));
endmodule

module ula_OR (
  input  [7:0] in_1,
  input  [7:0] in_2,
  output [7:0] out_3
);

  op_OR op_or_1 (.in_1(in_1[0]), .in_2(in_2[0]), .out_3(out_3[0]));
  op_OR op_or_2 (.in_1(in_1[1]), .in_2(in_2[1]), .out_3(out_3[1]));
  op_OR op_or_3 (.in_1(in_1[2]), .in_2(in_2[2]), .out_3(out_3[2]));
  op_OR op_or_4 (.in_1(in_1[3]), .in_2(in_2[3]), .out_3(out_3[3]));
  op_OR op_or_5 (.in_1(in_1[4]), .in_2(in_2[4]), .out_3(out_3[4]));
  op_OR op_or_6 (.in_1(in_1[5]), .in_2(in_2[5]), .out_3(out_3[5]));
  op_OR op_or_7 (.in_1(in_1[6]), .in_2(in_2[6]), .out_3(out_3[6]));
  op_OR op_or_8 (.in_1(in_1[7]), .in_2(in_2[7]), .out_3(out_3[7]));
endmodule

module ula_NAND (
  input  [7:0] in_1,
  input  [7:0] in_2,
  output [7:0] out_3
);

  op_NAND op_nand_1 (.in_1(in_1[0]), .in_2(in_2[0]), .out_3(out_3[0]));
  op_NAND op_nand_2 (.in_1(in_1[1]), .in_2(in_2[1]), .out_3(out_3[1]));
  op_NAND op_nand_3 (.in_1(in_1[2]), .in_2(in_2[2]), .out_3(out_3[2]));
  op_NAND op_nand_4 (.in_1(in_1[3]), .in_2(in_2[3]), .out_3(out_3[3]));
  op_NAND op_nand_5 (.in_1(in_1[4]), .in_2(in_2[4]), .out_3(out_3[4]));
  op_NAND op_nand_6 (.in_1(in_1[5]), .in_2(in_2[5]), .out_3(out_3[5]));
  op_NAND op_nand_7 (.in_1(in_1[6]), .in_2(in_2[6]), .out_3(out_3[6]));
  op_NAND op_nand_8 (.in_1(in_1[7]), .in_2(in_2[7]), .out_3(out_3[7]));
endmodule

module ula_SUB (
  input  [7:0] in_1,
  input  [7:0] in_2,
  output [7:0] out_3,
  output out_4
);

  wire not_1_out, not_2_out, not_3_out, not_4_out, not_5_out, not_6_out, not_7_out, not_8_out,
       op_add_1_out_5, op_add_2_out_5, op_add_3_out_5, op_add_4_out_5, op_add_5_out_5, op_add_6_out_5,
       op_add_7_out_5, op_add_8_out_5;

  not not_1 (not_1_out, in_2[0]);
  not not_2 (not_2_out, in_2[1]);
  not not_3 (not_3_out, in_2[2]);
  not not_4 (not_4_out, in_2[3]);
  not not_5 (not_5_out, in_2[4]);
  not not_6 (not_6_out, in_2[5]);
  not not_7 (not_7_out, in_2[6]);
  not not_8 (not_8_out, in_2[7]);
  op_ADD op_add_1 (.in_1(in_1[0]), .in_2(not_1_out), .Carry_In(1'b1), .out_4(out_3[0]), .out_5(op_add_1_out_5));
  op_ADD op_add_2 (
    .in_1(in_1[1]), .in_2(not_2_out), .Carry_In(op_add_1_out_5), .out_4(out_3[1]), .out_5(op_add_2_out_5));
  op_ADD op_add_3 (
    .in_1(in_1[2]), .in_2(not_3_out), .Carry_In(op_add_2_out_5), .out_4(out_3[2]), .out_5(op_add_3_out_5));
  op_ADD op_add_4 (
    .in_1(in_1[3]), .in_2(not_4_out), .Carry_In(op_add_3_out_5), .out_4(out_3[3]), .out_5(op_add_4_out_5));
  op_ADD op_add_5 (
    .in_1(in_1[4]), .in_2(not_5_out), .Carry_In(op_add_4_out_5), .out_4(out_3[4]), .out_5(op_add_5_out_5));
  op_ADD op_add_6 (
    .in_1(in_1[5]), .in_2(not_6_out), .Carry_In(op_add_5_out_5), .out_4(out_3[5]), .out_5(op_add_6_out_5));
  op_ADD op_add_7 (
    .in_1(in_1[6]), .in_2(not_7_out), .Carry_In(op_add_6_out_5), .out_4(out_3[6]), .out_5(op_add_7_out_5));
  op_ADD op_add_8 (
    .in_1(in_1[7]), .in_2(not_8_out), .Carry_In(op_add_7_out_5), .out_4(out_3[7]), .out_5(op_add_8_out_5));
  xor xor_1 (out_4, op_add_8_out_5, op_add_7_out_5);

  // Notes on the sheet:
  //   Overflow/Underflow
endmodule

module ula_mux (
  input  in_1,
  input  in_2,
  input  in_3,
  input  [7:0] in_4,
  input  [7:0] in_5,
  input  [7:0] in_6,
  input  [7:0] in_7,
  input  [7:0] in_8,
  input  [7:0] in_9,
  input  [7:0] in_10,
  input  [7:0] in_11,
  output [7:0] out_12
);

  mux_8x1 mux_8x1_1 (
    .in_1(in_4[0]), .in_2(in_5[0]), .in_3(in_6[0]), .in_4(in_7[0]), .in_5(in_8[0]), .in_6(in_9[0]),
    .in_7(in_10[0]), .in_8(in_11[0]), .in_9(in_1), .in_10(in_2), .in_11(in_3), .out_12(out_12[0]));
  mux_8x1 mux_8x1_2 (
    .in_1(in_4[1]), .in_2(in_5[1]), .in_3(in_6[1]), .in_4(in_7[1]), .in_5(in_8[1]), .in_6(in_9[1]),
    .in_7(in_10[1]), .in_8(in_11[1]), .in_9(in_1), .in_10(in_2), .in_11(in_3), .out_12(out_12[1]));
  mux_8x1 mux_8x1_3 (
    .in_1(in_4[2]), .in_2(in_5[2]), .in_3(in_6[2]), .in_4(in_7[2]), .in_5(in_8[2]), .in_6(in_9[2]),
    .in_7(in_10[2]), .in_8(in_11[2]), .in_9(in_1), .in_10(in_2), .in_11(in_3), .out_12(out_12[2]));
  mux_8x1 mux_8x1_4 (
    .in_1(in_4[3]), .in_2(in_5[3]), .in_3(in_6[3]), .in_4(in_7[3]), .in_5(in_8[3]), .in_6(in_9[3]),
    .in_7(in_10[3]), .in_8(in_11[3]), .in_9(in_1), .in_10(in_2), .in_11(in_3), .out_12(out_12[3]));
  mux_8x1 mux_8x1_5 (
    .in_1(in_4[4]), .in_2(in_5[4]), .in_3(in_6[4]), .in_4(in_7[4]), .in_5(in_8[4]), .in_6(in_9[4]),
    .in_7(in_10[4]), .in_8(in_11[4]), .in_9(in_1), .in_10(in_2), .in_11(in_3), .out_12(out_12[4]));
  mux_8x1 mux_8x1_6 (
    .in_1(in_4[5]), .in_2(in_5[5]), .in_3(in_6[5]), .in_4(in_7[5]), .in_5(in_8[5]), .in_6(in_9[5]),
    .in_7(in_10[5]), .in_8(in_11[5]), .in_9(in_1), .in_10(in_2), .in_11(in_3), .out_12(out_12[5]));
  mux_8x1 mux_8x1_7 (
    .in_1(in_4[6]), .in_2(in_5[6]), .in_3(in_6[6]), .in_4(in_7[6]), .in_5(in_8[6]), .in_6(in_9[6]),
    .in_7(in_10[6]), .in_8(in_11[6]), .in_9(in_1), .in_10(in_2), .in_11(in_3), .out_12(out_12[6]));
  mux_8x1 mux_8x1_8 (
    .in_1(in_4[7]), .in_2(in_5[7]), .in_3(in_6[7]), .in_4(in_7[7]), .in_5(in_8[7]), .in_6(in_9[7]),
    .in_7(in_10[7]), .in_8(in_11[7]), .in_9(in_1), .in_10(in_2), .in_11(in_3), .out_12(out_12[7]));

  // Notes on the sheet:
  //   Sel.Op
  //   Resultado Escolhido
endmodule

module flag_Z (
  input  [7:0] in_1,
  output out_2
);

  wire or_1_out, or_2_out, or_3_out, or_4_out, or_5_out, or_6_out, or_7_out;

  or or_1 (or_1_out, in_1[0], in_1[1]);
  or or_2 (or_2_out, in_1[2], in_1[3]);
  or or_3 (or_3_out, in_1[4], in_1[5]);
  or or_4 (or_4_out, in_1[6], in_1[7]);
  or or_5 (or_5_out, or_1_out, or_2_out);
  or or_6 (or_6_out, or_3_out, or_4_out);
  or or_7 (or_7_out, or_5_out, or_6_out);
  not not_1 (out_2, or_7_out);
endmodule
